// Logisim project Cache Memory.circ as structural Verilog: 1 circuit, main circuit main
module main (
  input  [31:0] RAM_In_0,
  input  Clk,
  input  Rst,
  input  R_W,
  input  [31:0] RAM_In_1,
  input  Find,
  input  [3:0] RT,
  input  [31:0] RAM_In_2,
  input  [31:0] RAM_In_3,
  input  [31:0] Address
);

  wire En_0, En_1, En_2, En_3;
  wire [13:0] Tag_0, Tag_1, Tag_2, Tag_3;
  wire [31:0] Out_0, Out_1, Out_2, Out_3, Out_4, Out_5, Out_6, Out_7, Out_8, Out_9, Out_10, Out_11, Out_12,
       Out_13, Out_14, Out_15;

  Register #(.width(14)) register_1 (.D(Address[19:6]), .en(En_0), .Q(Tag_0), .clk(Clk), .clr(Rst));
  Register #(.width(14)) register_2 (.D(Address[19:6]), .en(En_1), .Q(Tag_1), .clk(Clk), .clr(Rst));
  Register #(.width(14)) register_3 (.D(Address[19:6]), .en(En_2), .Q(Tag_2), .clk(Clk), .clr(Rst));
  Register #(.width(14)) register_4 (.D(Address[19:6]), .en(En_3), .Q(Tag_3), .clk(Clk), .clr(Rst));
  Register #(.width(32)) register_5 (.D(RAM_In_0), .en(En_0), .Q(Out_0), .clk(Clk), .clr(Rst));
  Register #(.width(32)) register_6 (.D(RAM_In_0), .en(En_1), .Q(Out_4), .clk(Clk), .clr(Rst));
  Register #(.width(32)) register_7 (.D(RAM_In_0), .en(En_2), .Q(Out_8), .clk(Clk), .clr(Rst));
  Register #(.width(32)) register_8 (.D(RAM_In_0), .en(En_3), .Q(Out_12), .clk(Clk), .clr(Rst));
  Register #(.width(32)) register_9 (.D(RAM_In_1), .en(En_0), .Q(Out_1), .clk(Clk), .clr(Rst));
  Register #(.width(32)) register_10 (.D(RAM_In_1), .en(En_1), .Q(Out_5), .clk(Clk), .clr(Rst));
  Register #(.width(32)) register_11 (.D(RAM_In_1), .en(En_2), .Q(Out_9), .clk(Clk), .clr(Rst));
  Register #(.width(32)) register_12 (.D(RAM_In_1), .en(En_3), .Q(Out_13), .clk(Clk), .clr(Rst));
  Register #(.width(32)) register_13 (.D(RAM_In_2), .en(En_0), .Q(Out_2), .clk(Clk), .clr(Rst));
  Register #(.width(32)) register_14 (.D(RAM_In_2), .en(En_1), .Q(Out_6), .clk(Clk), .clr(Rst));
  Register #(.width(32)) register_15 (.D(RAM_In_2), .en(En_2), .Q(Out_10), .clk(Clk), .clr(Rst));
  Register #(.width(32)) register_16 (.D(RAM_In_2), .en(En_3), .Q(Out_14), .clk(Clk), .clr(Rst));
  Register #(.width(32)) register_17 (.D(RAM_In_3), .en(En_0), .Q(Out_3), .clk(Clk), .clr(Rst));
  Register #(.width(32)) register_18 (.D(RAM_In_3), .en(En_1), .Q(Out_7), .clk(Clk), .clr(Rst));
  Register #(.width(32)) register_19 (.D(RAM_In_3), .en(En_2), .Q(Out_11), .clk(Clk), .clr(Rst));
  Register #(.width(32)) register_20 (.D(RAM_In_3), .en(En_3), .Q(Out_15), .clk(Clk), .clr(Rst));

  // Other names for the same wires on the sheet: Offset[1:0] = Address[3:2]; Index[1:0] = Address[5:4];
  //   R_Address[15:0] = Address[19:4]; Tag[13:0] = Address[19:6]; In_0[31:0] = RAM_In_0; In_1[31:0] = RAM_In_1;
  //   In_2[31:0] = RAM_In_2; In_3[31:0] = RAM_In_3

  // Notes on the sheet:
  //   Inputs
  //   Tags
  //   Memory
endmodule
