// Logisim project Data Path.circ as structural Verilog: 1 circuit, main circuit main
module main (
  input  [31:0] Data_In,
  input  Clock,
  input  Reset,
  input  [31:0] PC_prime,
  input  [4:0] RS,
  input  [4:0] RD,
  input  [15:0] Offset,
  input  [4:0] RT,
  input  Log_Inm_Op,
  input  [3:0] ALU_Op,
  input  Write_PC,
  input  [1:0] B_Selector,
  input  [2:0] DL_Selector,
  input  rt_rd,
  input  R_W,
  input  Push,
  input  Pop
);

  wire [31:0] PC;

  Register #(.width(32)) Program_Counter (.D(PC_prime), .en(Write_PC), .Q(PC), .clk(Clock), .clr(Reset));

  // Other names for the same wires on the sheet: Clk = Clock; Rst = Reset

  // Notes on the sheet:
  //   Inputs
  //   RAM
  //   Branch Control
  //   Instruction Decoder
  //   Control Unit
endmodule
