// Logisim project Operation Decoder.circ as structural Verilog: 1 circuit, main circuit Operation Decoder
module Operation_Decoder (
  input  [5:0] OP_Code,
  input  [5:0] FUNC_Code
);

  wire add, addi, ALU_OP, \and , and_11_out, and_13_out, and_15_out, and_17_out, and_19_out, and_21_out,
       and_29_out, and_31_out, and_32_out, and_33_out, and_34_out, and_35_out, and_36_out, and_45_out,
       and_46_out, and_47_out, and_51_out, and_52_out, and_55_out, and_56_out, and_57_out, and_58_out, andi,
       beq, bgtz, blez, bltz, bne, Branch_OP, div, divu, F_000000, halt, Immediate_OP, j, jr, kbd,
       Logical_Immediate_OP, lw, mfhi, mflo, mult, Mult_Div_OP, mulu, nop, \nor , OP_000000, OP_000111,
       OP_111111, \or , ori, pop, push, RAM_OP, Register_OP, rnd, sliti, slitiu, slt, sltu, Special_OP, sub,
       sw, tty, \xor , xori;

  // Probe on OP_Code
  // Probe on FUNC_Code
  and and_1 (OP_000000, ~OP_Code[0], ~OP_Code[1], ~OP_Code[2], ~OP_Code[3], ~OP_Code[4], ~OP_Code[5]);  // AND_Gate
  and and_2 (OP_000111, ~OP_Code[0], ~OP_Code[1], ~OP_Code[2], OP_Code[3], OP_Code[4], OP_Code[5]);  // AND_Gate
  and and_3 (OP_111111, OP_Code[0], OP_Code[1], OP_Code[2], OP_Code[3], OP_Code[4], OP_Code[5]);
  and and_4 (F_000000, ~FUNC_Code[0], ~FUNC_Code[1], ~FUNC_Code[2], ~FUNC_Code[3], ~FUNC_Code[4], ~FUNC_Code[5]);  // AND_Gate
  and and_5 (addi, ~OP_Code[0], ~OP_Code[1], ~OP_Code[2], OP_Code[3], ~OP_Code[4], ~OP_Code[5]);  // AND_Gate
  and and_6 (sliti, ~OP_Code[0], OP_Code[1], ~OP_Code[2], OP_Code[3], ~OP_Code[4], ~OP_Code[5]);  // AND_Gate
  and and_7 (slitiu, OP_Code[0], OP_Code[1], ~OP_Code[2], OP_Code[3], ~OP_Code[4], ~OP_Code[5]);  // AND_Gate
  and and_8 (andi, ~OP_Code[0], ~OP_Code[1], OP_Code[2], OP_Code[3], ~OP_Code[4], ~OP_Code[5]);  // AND_Gate
  and and_9 (ori, OP_Code[0], ~OP_Code[1], OP_Code[2], OP_Code[3], ~OP_Code[4], ~OP_Code[5]);  // AND_Gate
  and and_10 (xori, ~OP_Code[0], OP_Code[1], OP_Code[2], OP_Code[3], ~OP_Code[4], ~OP_Code[5]);  // AND_Gate
  and and_11 (and_11_out, ~FUNC_Code[0], ~FUNC_Code[1], ~FUNC_Code[2], ~FUNC_Code[3], ~FUNC_Code[4], FUNC_Code[5]);  // AND_Gate
  and and_12 (add, and_11_out, OP_000000);
  and and_13 (and_13_out, ~FUNC_Code[0], FUNC_Code[1], ~FUNC_Code[2], ~FUNC_Code[3], ~FUNC_Code[4], FUNC_Code[5]);  // AND_Gate
  and and_14 (sub, and_13_out, OP_000000);
  and and_15 (and_15_out, ~FUNC_Code[0], ~FUNC_Code[1], ~FUNC_Code[2], FUNC_Code[3], FUNC_Code[4], ~FUNC_Code[5]);  // AND_Gate
  and and_16 (mult, and_15_out, OP_000000);
  and and_17 (and_17_out, FUNC_Code[0], ~FUNC_Code[1], ~FUNC_Code[2], FUNC_Code[3], FUNC_Code[4], ~FUNC_Code[5]);  // AND_Gate
  and and_18 (mulu, and_17_out, OP_000000);
  and and_19 (and_19_out, ~FUNC_Code[0], FUNC_Code[1], ~FUNC_Code[2], FUNC_Code[3], FUNC_Code[4], ~FUNC_Code[5]);  // AND_Gate
  and and_20 (div, and_19_out, OP_000000);
  and and_21 (and_21_out, FUNC_Code[0], FUNC_Code[1], ~FUNC_Code[2], FUNC_Code[3], FUNC_Code[4], ~FUNC_Code[5]);  // AND_Gate
  and and_22 (divu, and_21_out, OP_000000);
  and and_23 (beq, ~OP_Code[0], ~OP_Code[1], OP_Code[2], ~OP_Code[3], ~OP_Code[4], ~OP_Code[5]);  // AND_Gate
  and and_24 (bne, OP_Code[0], ~OP_Code[1], OP_Code[2], ~OP_Code[3], ~OP_Code[4], ~OP_Code[5]);  // AND_Gate
  and and_25 (blez, ~OP_Code[0], OP_Code[1], OP_Code[2], ~OP_Code[3], ~OP_Code[4], ~OP_Code[5]);  // AND_Gate
  and and_26 (bgtz, OP_Code[0], OP_Code[1], OP_Code[2], ~OP_Code[3], ~OP_Code[4], ~OP_Code[5]);  // AND_Gate
  and and_27 (bltz, OP_Code[0], ~OP_Code[1], ~OP_Code[2], ~OP_Code[3], ~OP_Code[4], ~OP_Code[5]);  // AND_Gate
  and and_28 (j, ~OP_Code[0], OP_Code[1], ~OP_Code[2], ~OP_Code[3], ~OP_Code[4], ~OP_Code[5]);  // AND_Gate
  and and_29 (and_29_out, ~OP_Code[0], ~OP_Code[1], ~OP_Code[2], ~OP_Code[3], ~OP_Code[4], ~OP_Code[5]);  // AND_Gate
  and and_30 (nop, and_29_out, F_000000);
  and and_31 (and_31_out, ~FUNC_Code[0], ~FUNC_Code[1], FUNC_Code[2], ~FUNC_Code[3], ~FUNC_Code[4], FUNC_Code[5]);  // AND_Gate
  and and_32 (and_32_out, FUNC_Code[0], ~FUNC_Code[1], FUNC_Code[2], ~FUNC_Code[3], ~FUNC_Code[4], FUNC_Code[5]);  // AND_Gate
  and and_33 (and_33_out, FUNC_Code[0], FUNC_Code[1], FUNC_Code[2], ~FUNC_Code[3], ~FUNC_Code[4], FUNC_Code[5]);  // AND_Gate
  and and_34 (and_34_out, ~FUNC_Code[0], ~FUNC_Code[1], ~FUNC_Code[2], FUNC_Code[3], ~FUNC_Code[4], FUNC_Code[5]);  // AND_Gate
  and and_35 (and_35_out, ~FUNC_Code[0], FUNC_Code[1], ~FUNC_Code[2], FUNC_Code[3], ~FUNC_Code[4], FUNC_Code[5]);  // AND_Gate
  and and_36 (and_36_out, FUNC_Code[0], FUNC_Code[1], ~FUNC_Code[2], FUNC_Code[3], ~FUNC_Code[4], FUNC_Code[5]);  // AND_Gate
  and and_37 (\and , and_31_out, OP_000000);
  and and_38 (\or , and_32_out, OP_000000);
  and and_39 (\nor , and_33_out, OP_000000);
  and and_40 (\xor , and_34_out, OP_000000);
  and and_41 (slt, and_35_out, OP_000000);
  and and_42 (sltu, and_36_out, OP_000000);
  and and_43 (lw, OP_Code[0], OP_Code[1], ~OP_Code[2], ~OP_Code[3], ~OP_Code[4], OP_Code[5]);  // AND_Gate
  and and_44 (sw, OP_Code[0], OP_Code[1], ~OP_Code[2], OP_Code[3], ~OP_Code[4], OP_Code[5]);  // AND_Gate
  and and_45 (and_45_out, ~FUNC_Code[0], ~FUNC_Code[1], ~FUNC_Code[2], FUNC_Code[3], ~FUNC_Code[4], ~FUNC_Code[5]);  // AND_Gate
  and and_46 (and_46_out, ~FUNC_Code[0], ~FUNC_Code[1], ~FUNC_Code[2], ~FUNC_Code[3], FUNC_Code[4], ~FUNC_Code[5]);  // AND_Gate
  and and_47 (and_47_out, ~FUNC_Code[0], FUNC_Code[1], ~FUNC_Code[2], ~FUNC_Code[3], FUNC_Code[4], ~FUNC_Code[5]);  // AND_Gate
  or or_1 (ALU_OP, add, sub, mult, mulu, div, divu, slt, sltu, \and , \or , \nor , \xor );
  or or_2 (Branch_OP, nop, beq, bne, blez, bgtz, bltz, j, jr);
  or or_3 (Immediate_OP, addi, sliti, slitiu, andi, ori, xori);
  or or_4 (Logical_Immediate_OP, andi, ori, xori);
  and and_48 (jr, and_45_out, OP_000000);
  and and_49 (mfhi, and_46_out, OP_000000);
  and and_50 (mflo, and_47_out, OP_000000);
  or or_5 (Special_OP, halt, rnd, kbd, tty);
  or or_6 (Special_OP, pop, push);
  or or_7 (RAM_OP, lw, sw);
  or or_8 (Register_OP, mfhi, mflo);
  or or_9 (Mult_Div_OP, mult, mulu, div, divu);
  and and_51 (and_51_out, ~FUNC_Code[0], ~FUNC_Code[1], ~FUNC_Code[2], ~FUNC_Code[3], ~FUNC_Code[4], ~FUNC_Code[5]);  // AND_Gate
  and and_52 (and_52_out, FUNC_Code[0], ~FUNC_Code[1], ~FUNC_Code[2], ~FUNC_Code[3], ~FUNC_Code[4], ~FUNC_Code[5]);  // AND_Gate
  and and_53 (pop, and_51_out, OP_000111);
  and and_54 (push, and_52_out, OP_000111);
  and and_55 (and_55_out, FUNC_Code[0], FUNC_Code[1], FUNC_Code[2], FUNC_Code[3], FUNC_Code[4], FUNC_Code[5]);
  and and_56 (and_56_out, ~FUNC_Code[0], FUNC_Code[1], ~FUNC_Code[2], ~FUNC_Code[3], ~FUNC_Code[4], ~FUNC_Code[5]);  // AND_Gate
  and and_57 (and_57_out, ~FUNC_Code[0], ~FUNC_Code[1], FUNC_Code[2], ~FUNC_Code[3], ~FUNC_Code[4], ~FUNC_Code[5]);  // AND_Gate
  and and_58 (and_58_out, FUNC_Code[0], ~FUNC_Code[1], ~FUNC_Code[2], ~FUNC_Code[3], ~FUNC_Code[4], ~FUNC_Code[5]);  // AND_Gate
  and and_59 (halt, and_55_out, OP_111111);
  and and_60 (rnd, and_56_out, OP_111111);
  and and_61 (kbd, and_57_out, OP_111111);
  and and_62 (tty, and_58_out, OP_111111);

  // Notes on the sheet:
  //   INPUTS
  //   No Op
  //   TIpo R
  //   Push/Pop
  //   Specials
  //   ALU 
  //   ALU 
  //   Op Code Decode
  //   Branch
  //   RAM
  //   Registers
  //   Func Code Decode
  //   Operations
  //   Stacks
  //   Specials
endmodule
